# Fritzing sketch 4 - Connect the BMP180 (saved by Fritzing 0.9.2b)
breadboards: 1

parts:
  Part1 = Arduino Uno (Rev3) - ICSP
  CC3K1 = Adafruit CC3000 WiFi Breakout
  DHT1 = DHT11 Humitidy and Temperature Sensor
  R1 = Resistor [tolerance=±5% resistance=10k package=THT]
  BMP1 = BMP085 Breakout

nets:
  N1: Part1.A4/SDA, BMP1.SDA
  N2: Part1.A5/SCL, BMP1.SCL
  5V: Part1.5V, CC3K1.3V3, DHT1.VDD, R1.Pin_0, BMP1.VIN
  N3: Part1.D10_PWM/SS, CC3K1.CS
  N4: Part1.D11_PWM/MOSI, CC3K1.MOSI
  N5: Part1.D12/MISO, CC3K1.MISO
  N6: Part1.D13/SCK, CC3K1.CLK
  GND: Part1.GND, CC3K1.GND, DHT1.GND, BMP1.GND
  N7: Part1.D3_PWM, CC3K1.IRQ
  N8: Part1.D6_PWM, CC3K1.VBEN
  N9: Part1.D7, DHT1.DATA, R1.Pin_1
  N10: CC3K1.TXD, CC3K1.RXD

notes:
  Note: this says "BMP085 Sensor", but it is connected the same way as the BMP180

custom parts:
  Adafruit CC3000 WiFi Breakout: CC3000 WiFi Breakout
  DHT11 Humitidy and Temperature Sensor: DHT11 Humidity and Temperature Sensor
  BMP085 Breakout: A breakout for the BMP085 barometric pressure and temperature sensor
